// Logisim project RISCV.circ as structural Verilog
module main (
  output [31:0] S,
  output [31:0] out_2
);

  wire ALUSrc, CLK, IRWrite, isAUIPC, MARWrite, MDRWrite, MemWrite, PCWrite, RegWrite, RESET_CTR, Zero;
  wire [1:0] PCSrc, WBSrc;
  wire [2:0] Etat, funct3, ImmSrc;
  wire [3:0] ALUop;
  wire [4:0] rd, rs1, rs2;
  wire [6:0] funct7, opcode;
  wire [7:0] shifter_1_out;
  wire [23:0] shifter_1_out_2;
  wire [31:0] adder_1_out, adder_2_out, adder_3_out, DataRAM_dout, ImmExt, Instruction_RAM_dout, MAR_q,
       MDR_q, multiplexer_1_out, multiplexer_2_out, multiplexer_3_out, multiplexer_4_out, PC_old_q, PC_q,
       registerfile_1_p1, SB, shifter_2_out;

  Clock u_CLK (.out(CLK));
  Counter #(.max('h7), .ongoal("continue"), .width(3)) UC_Counter (
    .load(RESET_CTR), .D(3'b000), .count(1'b1), .Q(Etat), .clk(CLK));  // open: carry, up, clr
  RAM #(.asyncread("true"), .dataWidth(32), .\type ("nonvolatile")) Instruction_RAM (
    .addr(shifter_1_out), .oe(1'b1), .clk(CLK), .dout(Instruction_RAM_dout));  // open: we, din
  UC uc_1 (
    .opcode(opcode), .funct3(funct3), .funct7(funct7), .Etat(Etat), .Zero(Zero), .ALUResult(out_2[0]),
    .IRWrite(IRWrite), .MemWrite(MemWrite), .PCWrite(PCWrite), .RegWrite(RegWrite), .MARWrite(MARWrite),
    .MDRWrite(MDRWrite), .ALUSrc(ALUSrc), .ImmSrc(ImmSrc), .WBSrc(WBSrc), .PCSrc(PCSrc),
    .RESET_CTR(RESET_CTR), .ALUop(ALUop), .isAUIPC(isAUIPC));  // open: MemAddrSrc
  Register #(.width(32)) IR (
    .D(Instruction_RAM_dout), .en(IRWrite), .Q({funct7, rs2, rs1, funct3, rd, opcode}), .clk(CLK));  // open: clr
  Adder #(.width(32)) adder_1 (.a(PC_old_q), .b(ImmExt), .out(adder_1_out));  // open: cin, cout
  Multiplexer #(.enable("true"), .select(2), .width(32)) multiplexer_1 (
    .in0(adder_2_out), .in1(adder_1_out), .in2(out_2), .out(multiplexer_1_out), .sel(PCSrc));  // open: in3, en
  Register #(.width(32)) PC (.D(multiplexer_1_out), .en(PCWrite), .Q(PC_q), .clk(CLK));  // open: clr
  SignExtender signextender_1 (.IR({funct7, rs2, rs1, funct3, rd, opcode}), .ImmSrc(ImmSrc), .ImmExt(ImmExt));
  Register #(.width(32)) PC_old (.D(PC_q), .en(IRWrite), .Q(PC_old_q), .clk(CLK));  // open: clr
  Shifter #(.shift("lr"), .width(32)) shifter_1 (.in(PC_q), .\dist (5'b00010), .out({shifter_1_out_2, shifter_1_out}));
  Adder #(.width(32)) adder_2 (.a(PC_q), .b(32'h4), .out(adder_2_out));  // open: cin, cout
  Adder #(.width(32)) adder_3 (.a(PC_old_q), .b(32'h4), .out(adder_3_out));  // open: cin, cout
  // Probe on out_2
  Multiplexer #(.enable("true"), .select(2), .width(32)) multiplexer_2 (
    .in0(out_2), .in1(MDR_q), .in2(adder_3_out), .in3(ImmExt), .out(multiplexer_2_out), .sel(WBSrc));  // open: en
  // Probe on WBSrc
  Register #(.width(32)) MAR (.D(out_2), .en(MARWrite), .Q(MAR_q), .clk(CLK));  // open: clr
  Shifter #(.shift("lr"), .width(32)) shifter_2 (.in(MAR_q), .\dist (5'b00010), .out(shifter_2_out));
  RAM #(.dataWidth(32), .enables("line"), .\type ("nonvolatile")) DataRAM (
    .addr(shifter_2_out[7:0]), .we(MemWrite), .clk(CLK), .din(SB), .dout(DataRAM_dout));
  // RegisterFile registerfile_1: pin names not known; wires that end beside it: registerfile_1_p1, SB, out_2
  Multiplexer #(.width(32)) multiplexer_3 (
    .in0(registerfile_1_p1), .in1(PC_old_q), .out(multiplexer_3_out), .sel(isAUIPC));
  Multiplexer #(.enable("true"), .width(32)) multiplexer_4 (
    .in0(SB), .in1(ImmExt), .out(multiplexer_4_out), .sel(ALUSrc));  // open: en
  Register #(.width(32)) MDR (.D(DataRAM_dout), .en(MDRWrite), .Q(MDR_q), .clk(CLK));  // open: clr
  ALU alu_1 (.A(multiplexer_3_out), .B(multiplexer_4_out), .OP(ALUop), .S(out_2), .Zero(Zero));

  assign S = out_2;

  // Other names for the same wires on the sheet: ALUResult = out_2[0]
endmodule

module ALU (
  input  [31:0] A,
  input  [31:0] B,
  input  [3:0] OP,
  output [31:0] S,
  output Zero
);

  wire comparator_1_lt, comparator_2_lt;
  wire [4:0] bitselector_1_out;
  wire [31:0] adder_1_out, and_1_out, bit_extender_1_out, bit_extender_2_out, multiplier_1_out, or_1_out,
       shifter_1_out, shifter_2_out, shifter_3_out, subtractor_1_out, xor_1_out;

  // Probe on A
  // Probe on B
  BitSelector #(.group(5), .width(32)) bitselector_1 (.in(B), .out(bitselector_1_out), .sel(3'b000));
  // Probe on bitselector_1_out
  // Probe on bitselector_1_out
  Adder #(.width(32)) adder_1 (.a(A), .b(B), .out(adder_1_out));  // open: cin, cout
  Subtractor #(.width(32)) subtractor_1 (.a(A), .b(B), .out(subtractor_1_out));  // open: bin, bout
  assign and_1_out = A & B;  // AND_Gate and_1, 32 bits wide
  assign or_1_out = A | B;  // OR_Gate or_1, 32 bits wide
  assign xor_1_out = A ^ B;  // XOR_Gate xor_1, 32 bits wide
  Shifter #(.width(32)) shifter_1 (.in(A), .\dist (bitselector_1_out), .out(shifter_1_out));
  Shifter #(.shift("lr"), .width(32)) shifter_2 (.in(A), .\dist (bitselector_1_out), .out(shifter_2_out));
  Shifter #(.shift("ar"), .width(32)) shifter_3 (.in(A), .\dist (bitselector_1_out), .out(shifter_3_out));
  Comparator #(.width(32)) comparator_1 (.a(A), .b(B), .lt(comparator_1_lt));  // open: gt, eq
  Comparator #(.mode("unsigned"), .width(32)) comparator_2 (.a(A), .b(B), .lt(comparator_2_lt));  // open: gt, eq
  Multiplier #(.mode("twosComplement"), .width(32)) multiplier_1 (
    .a(A), .b(B), .out(multiplier_1_out));  // open: cin, cout
  assign bit_extender_1_out = {{31{1'b0}}, comparator_1_lt};  // Bit_Extender bit_extender_1
  assign bit_extender_2_out = {{31{1'b0}}, comparator_2_lt};  // Bit_Extender bit_extender_2
  Multiplexer #(.enable("true"), .select(4), .width(32)) multiplexer_1 (
    .in0(adder_1_out), .in1(subtractor_1_out), .in2(and_1_out), .in3(or_1_out), .in4(xor_1_out),
    .in5(shifter_1_out), .in6(shifter_2_out), .in7(shifter_3_out), .in8(bit_extender_1_out),
    .in9(bit_extender_2_out), .in10(multiplier_1_out), .in11({32{1'b0}}), .in12({32{1'b0}}),
    .in13({32{1'b0}}), .in14({32{1'b0}}), .in15({32{1'b0}}), .out(S), .sel(OP));  // open: en
  // Probe on OP
  // Probe on S
  nor nor_1 (Zero, S[0], S[1], S[2], S[3], S[4], S[5], S[6], S[7], S[8], S[9], S[10], S[11], S[12], S[13], S[14], S[15], S[16], S[17], S[18], S[19], S[20], S[21], S[22], S[23], S[24], S[25], S[26], S[27], S[28], S[29], S[30], S[31]);
endmodule

module Decoder_5_32 (
  input  [4:0] E,
  output S0,
  output S1,
  output S2,
  output S3,
  output S4,
  output S5,
  output S6,
  output S7,
  output S8,
  output S9,
  output S10,
  output S11,
  output S12,
  output S13,
  output S14,
  output S15,
  output S16,
  output S17,
  output S18,
  output S19,
  output S20,
  output S21,
  output S22,
  output S23,
  output S24,
  output S25,
  output S26,
  output S27,
  output S28,
  output S29,
  output S30,
  output S31
);

  wire not_1_out, not_2_out, not_3_out, not_4_out, not_5_out;

  // Probe on E
  not not_1 (not_1_out, E[4]);
  not not_2 (not_2_out, E[3]);
  not not_3 (not_3_out, E[2]);
  not not_4 (not_4_out, E[1]);
  not not_5 (not_5_out, E[0]);
  and and_1 (S0, not_5_out, not_4_out, not_3_out, not_2_out, not_1_out);
  and and_2 (S1, E[0], not_4_out, not_3_out, not_2_out, not_1_out);
  and and_3 (S2, not_5_out, E[1], not_3_out, not_2_out, not_1_out);
  and and_4 (S3, E[0], E[1], not_3_out, not_2_out, not_1_out);
  and and_5 (S4, not_5_out, not_4_out, E[2], not_2_out, not_1_out);
  and and_6 (S5, E[0], not_4_out, E[2], not_2_out, not_1_out);
  and and_7 (S6, not_5_out, E[1], E[2], not_2_out, not_1_out);
  and and_8 (S7, E[0], E[1], E[2], not_2_out, not_1_out);
  and and_9 (S8, not_5_out, not_4_out, not_3_out, E[3], not_1_out);
  and and_10 (S9, E[0], not_4_out, not_3_out, E[3], not_1_out);
  and and_11 (S10, not_5_out, E[1], not_3_out, E[3], not_1_out);
  and and_12 (S11, E[0], E[1], not_3_out, E[3], not_1_out);
  and and_13 (S12, not_5_out, not_4_out, E[2], E[3], not_1_out);
  and and_14 (S13, E[0], not_4_out, E[2], E[3], not_1_out);
  and and_15 (S14, not_5_out, E[1], E[2], E[3], not_1_out);
  and and_16 (S15, E[0], E[1], E[2], E[3], not_1_out);
  and and_17 (S16, not_5_out, not_4_out, not_3_out, not_2_out, E[4]);
  and and_18 (S17, E[0], not_4_out, not_3_out, not_2_out, E[4]);
  and and_19 (S18, not_5_out, E[1], not_3_out, not_2_out, E[4]);
  and and_20 (S19, E[0], E[1], not_3_out, not_2_out, E[4]);
  and and_21 (S20, not_5_out, not_4_out, E[2], not_2_out, E[4]);
  and and_22 (S21, E[0], not_4_out, E[2], not_2_out, E[4]);
  and and_23 (S22, not_5_out, E[1], E[2], not_2_out, E[4]);
  and and_24 (S23, E[0], E[1], E[2], not_2_out, E[4]);
  and and_25 (S24, not_5_out, not_4_out, not_3_out, E[3], E[4]);
  and and_26 (S25, E[0], not_4_out, not_3_out, E[3], E[4]);
  and and_27 (S26, not_5_out, E[1], not_3_out, E[3], E[4]);
  and and_28 (S27, E[0], E[1], not_3_out, E[3], E[4]);
  and and_29 (S28, not_5_out, not_4_out, E[2], E[3], E[4]);
  and and_30 (S29, E[0], not_4_out, E[2], E[3], E[4]);
  and and_31 (S30, not_5_out, E[1], E[2], E[3], E[4]);
  and and_32 (S31, E[0], E[1], E[2], E[3], E[4]);
endmodule

module RegisterFile (
  input  [31:0] Data,
  input  RegWrite,
  input  CLK,
  input  [4:0] rd,
  input  [4:0] rs1,
  input  [4:0] rs2,
  output [31:0] SA,
  output [31:0] S12,
  output [31:0] SB
);

  wire and_1_out, and_2_out, and_3_out, and_4_out, and_5_out, and_6_out, and_7_out, and_8_out, and_9_out,
       and_10_out, and_11_out, and_12_out, and_13_out, and_14_out, and_15_out, and_16_out, and_17_out,
       and_18_out, and_19_out, and_20_out, and_21_out, and_22_out, and_23_out, and_24_out, and_25_out,
       and_26_out, and_27_out, and_28_out, and_29_out, and_30_out, and_31_out, decoder_5_32_1_s1,
       decoder_5_32_1_s2, decoder_5_32_1_s3, decoder_5_32_1_s4, decoder_5_32_1_s5, decoder_5_32_1_s6,
       decoder_5_32_1_s7, decoder_5_32_1_s8, decoder_5_32_1_s9, decoder_5_32_1_s10, decoder_5_32_1_s11,
       decoder_5_32_1_s12, decoder_5_32_1_s13, decoder_5_32_1_s14, decoder_5_32_1_s15, decoder_5_32_1_s16,
       decoder_5_32_1_s17, decoder_5_32_1_s18, decoder_5_32_1_s19, decoder_5_32_1_s20, decoder_5_32_1_s21,
       decoder_5_32_1_s22, decoder_5_32_1_s23, decoder_5_32_1_s24, decoder_5_32_1_s25, decoder_5_32_1_s26,
       decoder_5_32_1_s27, decoder_5_32_1_s28, decoder_5_32_1_s29, decoder_5_32_1_s30, decoder_5_32_1_s31;
  wire [31:0] x0, x1, x2, x3, x4, x5, x6, x7, x8, x9, x11, x12, x13, x14, x15, x16, x17, x18, x19, x20, x21,
       x22, x23, x24, x25, x26, x27, x28, x29, x30, x31;

  Decoder_5_32 decoder_5_32_1 (
    .E(rd), .S1(decoder_5_32_1_s1), .S2(decoder_5_32_1_s2), .S3(decoder_5_32_1_s3), .S4(decoder_5_32_1_s4),
    .S5(decoder_5_32_1_s5), .S6(decoder_5_32_1_s6), .S7(decoder_5_32_1_s7), .S8(decoder_5_32_1_s8),
    .S9(decoder_5_32_1_s9), .S10(decoder_5_32_1_s10), .S11(decoder_5_32_1_s11), .S12(decoder_5_32_1_s12),
    .S13(decoder_5_32_1_s13), .S14(decoder_5_32_1_s14), .S15(decoder_5_32_1_s15), .S16(decoder_5_32_1_s16),
    .S17(decoder_5_32_1_s17), .S18(decoder_5_32_1_s18), .S19(decoder_5_32_1_s19), .S20(decoder_5_32_1_s20),
    .S21(decoder_5_32_1_s21), .S22(decoder_5_32_1_s22), .S23(decoder_5_32_1_s23), .S24(decoder_5_32_1_s24),
    .S25(decoder_5_32_1_s25), .S26(decoder_5_32_1_s26), .S27(decoder_5_32_1_s27), .S28(decoder_5_32_1_s28),
    .S29(decoder_5_32_1_s29), .S30(decoder_5_32_1_s30), .S31(decoder_5_32_1_s31));  // open: S0
  Register #(.width(32)) u_x0 (.D(Data), .en(1'b0), .Q(x0), .clk(CLK));  // open: clr
  Register #(.width(32)) u_x8 (.D(Data), .en(and_1_out), .Q(x8), .clk(CLK));  // open: clr
  and and_1 (and_1_out, RegWrite, decoder_5_32_1_s8);
  Register #(.width(32)) u_x16 (.D(Data), .en(and_2_out), .Q(x16), .clk(CLK));  // open: clr
  and and_2 (and_2_out, RegWrite, decoder_5_32_1_s16);
  Register #(.width(32)) u_x24 (.D(Data), .en(and_3_out), .Q(x24), .clk(CLK));  // open: clr
  and and_3 (and_3_out, RegWrite, decoder_5_32_1_s24);
  // Probe on x0
  // Probe on x8
  // Probe on x16
  // Probe on x24
  // Probe on x1
  Register #(.width(32)) u_x1 (.D(Data), .en(and_4_out), .Q(x1), .clk(CLK));  // open: clr
  and and_4 (and_4_out, RegWrite, decoder_5_32_1_s1);
  Register #(.width(32)) u_x9 (.D(Data), .en(and_5_out), .Q(x9), .clk(CLK));  // open: clr
  and and_5 (and_5_out, RegWrite, decoder_5_32_1_s9);
  Register #(.width(32)) u_x17 (.D(Data), .en(and_6_out), .Q(x17), .clk(CLK));  // open: clr
  and and_6 (and_6_out, RegWrite, decoder_5_32_1_s17);
  Register #(.width(32)) u_x25 (.D(Data), .en(and_7_out), .Q(x25), .clk(CLK));  // open: clr
  and and_7 (and_7_out, RegWrite, decoder_5_32_1_s25);
  // Probe on x9
  // Probe on x17
  // Probe on x25
  and and_8 (and_8_out, RegWrite, decoder_5_32_1_s2);
  and and_9 (and_9_out, RegWrite, decoder_5_32_1_s10);
  and and_10 (and_10_out, RegWrite, decoder_5_32_1_s18);
  and and_11 (and_11_out, RegWrite, decoder_5_32_1_s26);
  // Probe on x2
  Register #(.width(32)) u_x2 (.D(Data), .en(and_8_out), .Q(x2), .clk(CLK));  // open: clr
  // Probe on S12
  Register #(.width(32)) x10 (.D(Data), .en(and_9_out), .Q(S12), .clk(CLK));  // open: clr
  // Probe on x18
  Register #(.width(32)) u_x18 (.D(Data), .en(and_10_out), .Q(x18), .clk(CLK));  // open: clr
  // Probe on x26
  Register #(.width(32)) u_x26 (.D(Data), .en(and_11_out), .Q(x26), .clk(CLK));  // open: clr
  and and_12 (and_12_out, RegWrite, decoder_5_32_1_s3);
  and and_13 (and_13_out, RegWrite, decoder_5_32_1_s11);
  and and_14 (and_14_out, RegWrite, decoder_5_32_1_s19);
  and and_15 (and_15_out, RegWrite, decoder_5_32_1_s27);
  // Probe on x3
  Register #(.width(32)) u_x3 (.D(Data), .en(and_12_out), .Q(x3), .clk(CLK));  // open: clr
  // Probe on x11
  Register #(.width(32)) u_x11 (.D(Data), .en(and_13_out), .Q(x11), .clk(CLK));  // open: clr
  // Probe on x19
  Register #(.width(32)) u_x19 (.D(Data), .en(and_14_out), .Q(x19), .clk(CLK));  // open: clr
  // Probe on x27
  Register #(.width(32)) u_x27 (.D(Data), .en(and_15_out), .Q(x27), .clk(CLK));  // open: clr
  and and_16 (and_16_out, RegWrite, decoder_5_32_1_s4);
  and and_17 (and_17_out, RegWrite, decoder_5_32_1_s12);
  and and_18 (and_18_out, RegWrite, decoder_5_32_1_s20);
  and and_19 (and_19_out, RegWrite, decoder_5_32_1_s28);
  // Probe on x4
  Register #(.width(32)) u_x4 (.D(Data), .en(and_16_out), .Q(x4), .clk(CLK));  // open: clr
  // Probe on x12
  Register #(.width(32)) u_x12 (.D(Data), .en(and_17_out), .Q(x12), .clk(CLK));  // open: clr
  // Probe on x20
  Register #(.width(32)) u_x20 (.D(Data), .en(and_18_out), .Q(x20), .clk(CLK));  // open: clr
  // Probe on x28
  Register #(.width(32)) u_x28 (.D(Data), .en(and_19_out), .Q(x28), .clk(CLK));  // open: clr
  Register #(.width(32)) u_x5 (.D(Data), .en(and_20_out), .Q(x5), .clk(CLK));  // open: clr
  and and_20 (and_20_out, RegWrite, decoder_5_32_1_s5);
  Register #(.width(32)) u_x13 (.D(Data), .en(and_21_out), .Q(x13), .clk(CLK));  // open: clr
  and and_21 (and_21_out, RegWrite, decoder_5_32_1_s13);
  Register #(.width(32)) u_x21 (.D(Data), .en(and_22_out), .Q(x21), .clk(CLK));  // open: clr
  and and_22 (and_22_out, RegWrite, decoder_5_32_1_s21);
  Register #(.width(32)) u_x29 (.D(Data), .en(and_23_out), .Q(x29), .clk(CLK));  // open: clr
  and and_23 (and_23_out, RegWrite, decoder_5_32_1_s29);
  // Probe on x5
  // Probe on x13
  // Probe on x21
  // Probe on x29
  and and_24 (and_24_out, RegWrite, decoder_5_32_1_s6);
  and and_25 (and_25_out, RegWrite, decoder_5_32_1_s14);
  and and_26 (and_26_out, RegWrite, decoder_5_32_1_s22);
  and and_27 (and_27_out, RegWrite, decoder_5_32_1_s30);
  // Probe on x6
  Register #(.width(32)) u_x6 (.D(Data), .en(and_24_out), .Q(x6), .clk(CLK));  // open: clr
  Register #(.width(32)) u_x14 (.D(Data), .en(and_25_out), .Q(x14), .clk(CLK));  // open: clr
  // Probe on x22
  Register #(.width(32)) u_x22 (.D(Data), .en(and_26_out), .Q(x22), .clk(CLK));  // open: clr
  // Probe on x30
  Register #(.width(32)) u_x30 (.D(Data), .en(and_27_out), .Q(x30), .clk(CLK));  // open: clr
  // Probe on x14
  and and_28 (and_28_out, RegWrite, decoder_5_32_1_s7);
  and and_29 (and_29_out, RegWrite, decoder_5_32_1_s15);
  and and_30 (and_30_out, RegWrite, decoder_5_32_1_s23);
  and and_31 (and_31_out, RegWrite, decoder_5_32_1_s31);
  // Probe on x7
  Register #(.width(32)) u_x7 (.D(Data), .en(and_28_out), .Q(x7), .clk(CLK));  // open: clr
  // Probe on x15
  Register #(.width(32)) u_x15 (.D(Data), .en(and_29_out), .Q(x15), .clk(CLK));  // open: clr
  Register #(.width(32)) u_x23 (.D(Data), .en(and_30_out), .Q(x23), .clk(CLK));  // open: clr
  Register #(.width(32)) u_x31 (.D(Data), .en(and_31_out), .Q(x31), .clk(CLK));  // open: clr
  // Probe on x23
  // Probe on x31
  Multiplexer #(.enable("true"), .select(5), .width(32)) multiplexer_1 (
    .in0(x0), .in1(x1), .in2(x2), .in3(x3), .in4(x4), .in5(x5), .in6(x6), .in7(x7), .in8(x8), .in9(x9),
    .in10(S12), .in11(x11), .in12(x12), .in13(x13), .in14(x14), .in15(x15), .in16(x16), .in17(x17),
    .in18(x18), .in19(x19), .in20(x20), .in21(x21), .in22(x22), .in23(x23), .in24(x24), .in25(x25),
    .in26(x26), .in27(x27), .in28(x28), .in29(x29), .in30(x30), .in31(x31), .out(SA), .sel(rs1));  // open: en
  Multiplexer #(.enable("true"), .select(5), .width(32)) multiplexer_2 (
    .in0(x0), .in1(x1), .in2(x2), .in3(x3), .in4(x4), .in5(x5), .in6(x6), .in7(x7), .in8(x8), .in9(x9),
    .in10(S12), .in11(x11), .in12(x12), .in13(x13), .in14(x14), .in15(x15), .in16(x16), .in17(x17),
    .in18(x18), .in19(x19), .in20(x20), .in21(x21), .in22(x22), .in23(x23), .in24(x24), .in25(x25),
    .in26(x26), .in27(x27), .in28(x28), .in29(x29), .in30(x30), .in31(x31), .out(SB), .sel(rs2));  // open: en

  // Other names for the same wires on the sheet: S10[31:0] = S12; x10[31:0] = S12

  // Notes on the sheet:
  //   x0 hardwired to 0 -> no enable 
endmodule

module SignExtender (
  input  [31:0] IR,
  input  [2:0] ImmSrc,
  output [31:0] ImmExt
);

  wire [31:0] bit_extender_1_out, bit_extender_2_out, bit_extender_3_out, bit_extender_4_out;

  assign bit_extender_1_out = {{20{IR[31]}}, IR[31:20]};  // Bit_Extender bit_extender_1
  assign bit_extender_2_out = {{20{IR[31]}}, {IR[31:25], IR[11:7]}};  // Bit_Extender bit_extender_2
  assign bit_extender_3_out = {{19{IR[31]}}, {IR[31], IR[7], IR[30:25], IR[11:8], 1'b0}};  // Bit_Extender bit_extender_3
  assign bit_extender_4_out = {{11{IR[31]}}, {IR[31], IR[19:12], IR[20], IR[30:21], 1'b0}};  // Bit_Extender bit_extender_4
  Multiplexer #(.enable("true"), .select(3), .width(32)) multiplexer_1 (
    .in0(bit_extender_1_out), .in1(bit_extender_2_out), .in2(bit_extender_3_out),
    .in3({IR[31:12], {12{1'b0}}}), .in4(bit_extender_4_out), .in5({32{1'b0}}), .in6({32{1'b0}}),
    .in7({32{1'b0}}), .out(ImmExt), .sel(ImmSrc));  // open: en

  // Notes on the sheet:
  //   Type I
  //   Type S
  //   Type B
  //   Type U
  //   Type J
endmodule

module Tetris (
  output [31:0] S,
  output [31:0] out_2
);

  wire ALUSrc, and_1_out, and_3_out, and_4_out, and_5_out, and_6_out, and_7_out, and_8_out, and_9_out,
       and_10_out, and_11_out, and_12_out, CLK, comparator_2_eq, comparator_2_gt, comparator_3_eq,
       comparator_3_lt, IRWrite, isAUIPC, MARWrite, MDRWrite, MemWrite, or_1_out, or_2_out, or_3_out,
       PCWrite, RegWrite, RESET_CTR, sel_counter, sel_joystick, sel_led, sel_led_col0, sel_led_col1,
       sel_led_col2, sel_led_col3, sel_led_col4, sel_led_col5, sel_led_col6, sel_led_col7, sel_led_col8,
       sel_led_col9, sel_ram, Zero;
  wire [1:0] PCSrc, WBSrc;
  wire [2:0] Etat, funct3, ImmSrc;
  wire [3:0] ALUop, button_input;
  wire [4:0] rd, rs1, rs2;
  wire [6:0] funct7, opcode;
  wire [7:0] shifter_1_out;
  wire [19:0] register_1_q, register_2_q, register_3_q, register_4_q, register_5_q, register_6_q,
       register_7_q, register_8_q, register_9_q, register_10_q;
  wire [23:0] shifter_1_out_2;
  wire [31:0] adder_1_out, adder_2_out, adder_3_out, counter_1_q, DataRAM_dout, ImmExt, Instruction_RAM_dout,
       MAR_q, MDR_q, multiplexer_1_out, multiplexer_2_out, multiplexer_3_out, multiplexer_4_out,
       multiplexer_5_out, PC_old_q, PC_q, registerfile_1_p1, SB, shifter_2_out, shifter_3_out,
       subtractor_1_out;

  Clock u_CLK (.out(CLK));
  Counter #(.max('h7), .ongoal("continue"), .width(3)) UC_Counter (
    .load(RESET_CTR), .D(3'b000), .count(1'b1), .Q(Etat), .clk(CLK));  // open: carry, up, clr
  RAM #(.asyncread("true"), .dataWidth(32), .\type ("nonvolatile")) Instruction_RAM (
    .addr(shifter_1_out), .oe(1'b1), .clk(CLK), .dout(Instruction_RAM_dout));  // open: we, din
  UC uc_1 (
    .opcode(opcode), .funct3(funct3), .funct7(funct7), .Etat(Etat), .Zero(Zero), .ALUResult(out_2[0]),
    .IRWrite(IRWrite), .MemWrite(MemWrite), .PCWrite(PCWrite), .RegWrite(RegWrite), .MARWrite(MARWrite),
    .MDRWrite(MDRWrite), .ALUSrc(ALUSrc), .ImmSrc(ImmSrc), .WBSrc(WBSrc), .PCSrc(PCSrc),
    .RESET_CTR(RESET_CTR), .ALUop(ALUop), .isAUIPC(isAUIPC));  // open: MemAddrSrc
  Register #(.width(32)) IR (
    .D(Instruction_RAM_dout), .en(IRWrite), .Q({funct7, rs2, rs1, funct3, rd, opcode}), .clk(CLK));  // open: clr
  Adder #(.width(32)) adder_1 (.a(PC_old_q), .b(ImmExt), .out(adder_1_out));  // open: cin, cout
  Multiplexer #(.enable("true"), .select(2), .width(32)) multiplexer_1 (
    .in0(adder_2_out), .in1(adder_1_out), .in2(out_2), .out(multiplexer_1_out), .sel(PCSrc));  // open: in3, en
  Register #(.width(32)) PC (.D(multiplexer_1_out), .en(PCWrite), .Q(PC_q), .clk(CLK));  // open: clr
  SignExtender signextender_1 (.IR({funct7, rs2, rs1, funct3, rd, opcode}), .ImmSrc(ImmSrc), .ImmExt(ImmExt));
  Register #(.width(32)) PC_old (.D(PC_q), .en(IRWrite), .Q(PC_old_q), .clk(CLK));  // open: clr
  Shifter #(.shift("lr"), .width(32)) shifter_1 (.in(PC_q), .\dist (5'b00010), .out({shifter_1_out_2, shifter_1_out}));
  Adder #(.width(32)) adder_2 (.a(PC_q), .b(32'h4), .out(adder_2_out));  // open: cin, cout
  Adder #(.width(32)) adder_3 (.a(PC_old_q), .b(32'h4), .out(adder_3_out));  // open: cin, cout
  // Probe on out_2
  Multiplexer #(.enable("true"), .select(2), .width(32)) multiplexer_2 (
    .in0(out_2), .in1(MDR_q), .in2(adder_3_out), .in3(ImmExt), .out(multiplexer_2_out), .sel(WBSrc));  // open: en
  // Probe on WBSrc
  Register #(.width(32)) MAR (.D(out_2), .en(MARWrite), .Q(MAR_q), .clk(CLK));  // open: clr
  Subtractor #(.width(32)) subtractor_1 (.a(MAR_q), .b(32'h104), .out(subtractor_1_out));  // open: bin, bout
  Shifter #(.shift("lr"), .width(32)) shifter_2 (.in(MAR_q), .\dist (5'b00010), .out(shifter_2_out));
  and and_1 (and_1_out, MemWrite, sel_ram);
  Comparator #(.width(32)) comparator_1 (.a(MAR_q), .b(32'h100), .eq(sel_joystick));  // open: gt, lt
  Comparator #(.width(32)) comparator_2 (
    .a(MAR_q), .b(32'h104), .gt(comparator_2_gt), .eq(comparator_2_eq));  // open: lt
  Comparator #(.width(32)) comparator_3 (
    .a(MAR_q), .b(32'h128), .eq(comparator_3_eq), .lt(comparator_3_lt));  // open: gt
  Comparator #(.width(32)) comparator_4 (.a(MAR_q), .b(32'h12c), .eq(sel_counter));  // open: gt, lt
  or or_1 (or_1_out, comparator_2_gt, comparator_2_eq);
  and and_2 (sel_led, or_1_out, or_2_out);
  or or_2 (or_2_out, comparator_3_eq, comparator_3_lt);
  Shifter #(.shift("lr"), .width(32)) shifter_3 (.in(subtractor_1_out), .\dist (5'b00010), .out(shifter_3_out));
  RAM #(.dataWidth(32), .enables("line"), .\type ("nonvolatile")) DataRAM (
    .addr(shifter_2_out[7:0]), .we(and_1_out), .clk(CLK), .din(SB), .dout(DataRAM_dout));
  or or_3 (or_3_out, sel_joystick, sel_counter, sel_led);
  not not_1 (sel_ram, or_3_out);
  Decoder #(.select(4)) decoder_1 (
    .out0(sel_led_col0), .out1(sel_led_col1), .out2(sel_led_col2), .out3(sel_led_col3), .out4(sel_led_col4),
    .out5(sel_led_col5), .out6(sel_led_col6), .out7(sel_led_col7), .out8(sel_led_col8), .out9(sel_led_col9),
    .sel(shifter_3_out[3:0]), .en(sel_led));  // open: out10, out11, out12, out13, out14, out15
  Counter #(.max('hffffffff), .width(32)) counter_1 (
    .Q(counter_1_q), .clk(CLK));  // open: load, D, count, carry, up, clr
  // RegisterFile registerfile_1: pin names not known; wires that end beside it: registerfile_1_p1, SB, out_2
  Multiplexer #(.width(32)) multiplexer_3 (
    .in0(registerfile_1_p1), .in1(PC_old_q), .out(multiplexer_3_out), .sel(isAUIPC));
  Multiplexer #(.enable("true"), .width(32)) multiplexer_4 (
    .in0(SB), .in1(ImmExt), .out(multiplexer_4_out), .sel(ALUSrc));  // open: en
  Multiplexer #(.select(2), .width(32)) multiplexer_5 (
    .in0(DataRAM_dout), .in1({{28{1'b0}}, button_input}), .in2(counter_1_q), .in3({32{1'b0}}),
    .out(multiplexer_5_out), .sel({sel_counter, sel_joystick}));
  Register #(.width(32)) MDR (.D(multiplexer_5_out), .en(MDRWrite), .Q(MDR_q), .clk(CLK));  // open: clr
  ALU alu_1 (.A(multiplexer_3_out), .B(multiplexer_4_out), .OP(ALUop), .S(out_2), .Zero(Zero));
  and and_3 (and_3_out, MemWrite, sel_led, sel_led_col0);
  and and_4 (and_4_out, MemWrite, sel_led, sel_led_col1);
  and and_5 (and_5_out, MemWrite, sel_led, sel_led_col2);
  and and_6 (and_6_out, MemWrite, sel_led, sel_led_col3);
  and and_7 (and_7_out, MemWrite, sel_led, sel_led_col4);
  and and_8 (and_8_out, MemWrite, sel_led, sel_led_col5);
  and and_9 (and_9_out, MemWrite, sel_led, sel_led_col6);
  and and_10 (and_10_out, MemWrite, sel_led, sel_led_col7);
  and and_11 (and_11_out, MemWrite, sel_led, sel_led_col8);
  and and_12 (and_12_out, MemWrite, sel_led, sel_led_col9);
  Register #(.width(20)) register_1 (.D(SB[19:0]), .en(and_3_out), .Q(register_1_q), .clk(CLK));  // open: clr
  Register #(.width(20)) register_2 (.D(SB[19:0]), .en(and_4_out), .Q(register_2_q), .clk(CLK));  // open: clr
  Register #(.width(20)) register_3 (.D(SB[19:0]), .en(and_5_out), .Q(register_3_q), .clk(CLK));  // open: clr
  Register #(.width(20)) register_4 (.D(SB[19:0]), .en(and_6_out), .Q(register_4_q), .clk(CLK));  // open: clr
  Register #(.width(20)) register_5 (.D(SB[19:0]), .en(and_7_out), .Q(register_5_q), .clk(CLK));  // open: clr
  Register #(.width(20)) register_6 (.D(SB[19:0]), .en(and_8_out), .Q(register_6_q), .clk(CLK));  // open: clr
  Register #(.width(20)) register_7 (.D(SB[19:0]), .en(and_9_out), .Q(register_7_q), .clk(CLK));  // open: clr
  Register #(.width(20)) register_8 (.D(SB[19:0]), .en(and_10_out), .Q(register_8_q), .clk(CLK));  // open: clr
  Register #(.width(20)) register_9 (.D(SB[19:0]), .en(and_11_out), .Q(register_9_q), .clk(CLK));  // open: clr
  Register #(.width(20)) register_10 (.D(SB[19:0]), .en(and_12_out), .Q(register_10_q), .clk(CLK));  // open: clr
  DotMatrix #(.matrixcols(10), .matrixrows(20)) dotmatrix_1 (
    .col0(register_1_q), .col1(register_2_q), .col2(register_3_q), .col3(register_4_q), .col4(register_5_q),
    .col5(register_6_q), .col6(register_7_q), .col7(register_8_q), .col8(register_9_q), .col9(register_10_q));
  Button button_1 (.out(button_input[2]));
  Button button_2 (.out(button_input[0]));
  Button button_3 (.out(button_input[3]));
  // Probe on {{28{1'b0}}, button_input}
  Button button_4 (.out(button_input[1]));

  assign S = out_2;

  // Other names for the same wires on the sheet: ALUResult = out_2[0]

  // Notes on the sheet:
  //   sel_joystick
  //   sel_led
endmodule

module frequency_divider (
  output [3:0] out_1
);

  wire clock_1_out;

  Clock clock_1 (.out(clock_1_out));
  Counter #(.max('hf), .width(4)) counter_1 (.Q(out_1), .clk(clock_1_out));  // open: load, D, count, carry, up, clr
  // Digital_Oscilloscope #(.nState(35)) digital_oscilloscope_1: pin names not known; wires that end beside it: clock_1_out, out_1[0], out_1[1], out_1[2], out_1[3]
endmodule

module front_detector (
);

  wire btn_any, btn_prev, CLK, irq_ext, not_1_out;
  wire [3:0] button_input;

  Clock clock_1 (.out(CLK));
  Button button_1 (.out(button_input[0]));
  Button button_2 (.out(button_input[2]));
  Button button_3 (.out(button_input[1]));
  Button button_4 (.out(button_input[3]));
  // Probe on {{28{1'b0}}, button_input}
  or or_1 (btn_any, button_input[1], button_input[0], button_input[3], button_input[2]);
  Register #(.width(1)) register_1 (.D(btn_any), .Q(btn_prev), .clk(CLK));  // open: en, clr
  not not_1 (not_1_out, btn_prev);
  and and_1 (irq_ext, not_1_out, btn_any);
endmodule

module UC (
  input  [6:0] opcode,
  input  [2:0] funct3,
  input  [6:0] funct7,
  input  [2:0] Etat,
  input  Zero,
  input  ALUResult,
  output IRWrite,
  output MemWrite,
  output PCWrite,
  output RegWrite,
  output MARWrite,
  output MDRWrite,
  output ALUSrc,
  output [2:0] ImmSrc,
  output [1:0] WBSrc,
  output [1:0] PCSrc,
  output RESET_CTR,
  output [3:0] ALUop,
  output isAUIPC,
  output MemAddrSrc
);

  wire and_2_out, and_3_out, and_4_out, and_5_out, and_6_out, and_7_out, and_8_out, and_10_out, and_11_out,
       and_12_out, and_13_out, and_14_out, and_15_out, and_16_out, and_17_out, and_18_out, and_19_out,
       and_20_out, and_21_out, and_22_out, and_23_out, and_24_out, and_26_out, and_27_out, and_28_out,
       and_29_out, and_32_out, branch_condition, branch_taken, isBEQ_BNE, isBLT_BGE, isBLTU_BGEU, isBranch,
       isJAL, isJALR, isLUI, isLW, isMUL, isState1, isState2, isState3, isState5, isSW, isTypeICalc, isTypeR,
       not_1_out, or_7_out, raw_condition;
  wire [0:0] or_10_out;
  wire [2:0] multiplexer_2_out;
  wire [3:0] ALUop_t, multiplexer_5_out, multiplexer_6_out;
  wire [3:3] multiplexer_1_out;

  Decoder #(.select(3)) decoder_1 (
    .out0(IRWrite), .out1(isState1), .out2(isState2), .out3(isState3), .out4(MemAddrSrc), .sel(Etat),
    .en(1'b1));  // open: out5, out6, out7
  Comparator #(.width(7)) comparator_1 (.a(opcode), .b(7'b0110011), .eq(isTypeR));  // open: gt, lt
  // Probe on 7'b0110011
  Comparator #(.width(7)) comparator_2 (.a(opcode), .b(7'b0010011), .eq(isTypeICalc));  // open: gt, lt
  // Probe on 7'b0010011
  Comparator #(.width(7)) comparator_3 (.a(opcode), .b(7'b0000011), .eq(isLW));  // open: gt, lt
  // Probe on 7'b0000011
  Comparator #(.width(7)) comparator_4 (.a(opcode), .b(7'b0100011), .eq(isSW));  // open: gt, lt
  // Probe on 7'b0100011
  Comparator #(.width(7)) comparator_5 (.a(opcode), .b(7'b1100011), .eq(isBranch));  // open: gt, lt
  // Probe on 7'b1100011
  Comparator #(.width(7)) comparator_6 (.a(opcode), .b(7'b1101111), .eq(isJAL));  // open: gt, lt
  // Probe on 7'b1101111
  Comparator #(.width(7)) comparator_7 (.a(opcode), .b(7'b1100111), .eq(isJALR));  // open: gt, lt
  // Probe on 7'b1100111
  Comparator #(.width(7)) comparator_8 (.a(opcode), .b(7'b0110111), .eq(isLUI));  // open: gt, lt
  // Probe on 7'b0110111
  Comparator #(.width(7)) comparator_9 (.a(opcode), .b(7'b0010111), .eq(isAUIPC));  // open: gt, lt
  // Probe on 7'b0010111
  and and_1 (isMUL, isTypeR, funct7[0]);
  Multiplexer multiplexer_1 (.in0(1'b0), .in1(funct7[5]), .out(multiplexer_1_out[3]), .sel(isTypeR));
  and and_2 (and_2_out, isTypeR, MemAddrSrc);
  and and_3 (and_3_out, MemAddrSrc, isTypeICalc);
  and and_4 (and_4_out, isState5, isLW);
  and and_5 (and_5_out, isState3, isJAL);
  and and_6 (and_6_out, MemAddrSrc, isJALR);
  and and_7 (and_7_out, isState3, isLUI);
  and and_8 (and_8_out, MemAddrSrc, isAUIPC);
  and and_9 (MDRWrite, MemAddrSrc, isLW);
  and and_10 (and_10_out, isState3, isLUI);
  and and_11 (and_11_out, isState3, isJAL);
  and and_12 (and_12_out, MemAddrSrc, isJALR);
  and and_13 (and_13_out, isState3, isLUI);
  and and_14 (and_14_out, isTypeR, MemAddrSrc);
  and and_15 (and_15_out, MemAddrSrc, isTypeICalc);
  and and_16 (and_16_out, isState5, isLW);
  and and_17 (and_17_out, MemAddrSrc, isSW);
  and and_18 (and_18_out, isState3, isBranch);
  and and_19 (and_19_out, isState3, isJAL);
  and and_20 (and_20_out, MemAddrSrc, isJALR);
  and and_21 (and_21_out, isState3, isLUI);
  and and_22 (and_22_out, MemAddrSrc, isAUIPC);
  ROM #(.addrWidth(4), .dataWidth(4)) rom_1 (.addr({multiplexer_1_out[3], funct3}), .data(ALUop_t));
  or or_1 (RegWrite, and_2_out, and_3_out, and_4_out, and_5_out, and_6_out, and_7_out, and_8_out);
  or or_2 (ALUSrc, 1'b0, isTypeICalc, isLW, isSW, isJALR, isAUIPC);
  and and_23 (and_23_out, isState5, isLW);
  or or_3 (WBSrc[0], and_10_out, and_23_out);
  or or_4 (WBSrc[1], and_11_out, and_12_out, and_13_out);
  or or_5 (RESET_CTR, and_14_out, and_15_out, and_16_out, and_17_out, and_18_out, and_19_out, and_20_out, and_21_out, and_22_out);
  // Probe on ALUop_t
  and and_24 (and_24_out, isBranch, isState3, branch_taken);
  Multiplexer #(.select(3), .width(3)) multiplexer_2 (
    .in0(3'b000), .in1(3'b001), .in2(3'b010), .in3(3'b011), .in4(3'b100), .out(multiplexer_2_out),
    .sel({isJAL, isBranch, isSW}));  // open: in5, in6, in7
  and and_25 (MemWrite, MemAddrSrc, isSW);
  and and_26 (and_26_out, isJAL, isState3);
  and and_27 (and_27_out, isJALR, MemAddrSrc);
  and and_28 (and_28_out, isState3, isLW);
  or or_6 (MARWrite, and_28_out, and_29_out);
  and and_29 (and_29_out, isState3, isSW);
  Multiplexer #(.width(3)) multiplexer_3 (.in0(multiplexer_2_out), .in1(3'b011), .out(ImmSrc), .sel(or_7_out));
  or or_7 (or_7_out, isAUIPC, isLUI);
  and and_30 (PCSrc[1], isJALR, MemAddrSrc);
  Multiplexer multiplexer_4 (.in0(Zero), .in1(ALUResult), .out(raw_condition), .sel(funct3[2]));
  xor xor_1 (branch_condition, raw_condition, funct3[0]);
  and and_31 (branch_taken, isBranch, isState3, branch_condition);
  or or_8 (PCSrc[0], branch_taken, and_32_out);
  and and_32 (and_32_out, isState3, isJAL);
  or or_9 (PCWrite, isState1, and_24_out, and_26_out, and_27_out);
  Multiplexer #(.select(2), .width(4)) multiplexer_5 (
    .in0(ALUop_t), .in1(4'b0000), .in2(4'b0001), .in3(4'b1000), .out(multiplexer_5_out),
    .sel({isBEQ_BNE, or_10_out[0]}));
  Multiplexer #(.width(4)) multiplexer_6 (
    .in0(multiplexer_5_out), .in1(4'b1001), .out(multiplexer_6_out), .sel(isBLTU_BGEU));
  or or_10 (or_10_out[0], isLW, isSW, isJALR, isAUIPC);
  not not_1 (not_1_out, funct3[2]);
  Multiplexer #(.width(4)) multiplexer_7 (.in0(multiplexer_6_out), .in1(4'b1010), .out(ALUop), .sel(isMUL));
  and and_33 (isBEQ_BNE, not_1_out, isBranch);
  and and_34 (isBLT_BGE, funct3[2], isBranch);
  and and_35 (isBLTU_BGEU, funct3[2], funct3[1], isBranch);

  // Other names for the same wires on the sheet: funct3_0 = funct3[0]; funct3_1 = funct3[1]; funct3_2 = funct3[2];
  //   funct7bit25 = funct7[0]; funct7bit30 = funct7[5]; isState0 = IRWrite; isState4 = MemAddrSrc;
  //   jump_taken = PCSrc[0]

  // Notes on the sheet:
  //   Fetch
  //   Decode
  //   isMUL has same opcode as type R
  //   isState0 (Fetch)
  //   Execute
  //   isTypeR
  //   isTypeI
  //   isLW
  //   isSW
  //   isBranch
  //   isJAL
  //   isJALR
  //   isLUI
  //   isAUIPC
  //   Memory
  //   Writeback
  //   contents of rom_1 (hex, n*v repeats v):
  //   0 5 8 9 4 6 3 2 1 4*0 7
endmodule

module CSR_File (
  input  [11:0] csr_addr,
  input  [31:0] DataIn,
  input  [2:0] funct3,
  input  write,
  input  CLK,
  input  irq_ext,
  input  irq_timer,
  input  [31:0] trac_pc,
  input  trap,
  input  mret,
  output mstatus_MIE,
  output irq_pending,
  output [31:0] mtvec_out,
  output [31:0] DataOut,
  output [31:0] mepc_out
);

  wire and_1_out, and_2_out, and_3_out, and_4_out, and_5_out, and_6_out, and_7_out, MEIE, MPIE_cur, MTIE,
       or_1_out, or_2_out, or_3_out, sel_mcause, sel_mepc, sel_mie, sel_mstatus, sel_mtvec;
  wire [1:0] or_6_out;
  wire [31:0] AND_result, DataIn_computed, mstatus_mret, multiplexer_1_out, multiplexer_2_out,
       multiplexer_3_out, multiplexer_4_out, not_1_out, OR_result, reg_mcause_Q, reg_mie_Q;

  Comparator #(.width(12)) comparator_1 (.a(csr_addr), .b(12'h300), .eq(sel_mstatus));  // open: gt, lt
  Comparator #(.width(12)) comparator_2 (.a(csr_addr), .b(12'h304), .eq(sel_mie));  // open: gt, lt
  Comparator #(.width(12)) comparator_3 (.a(csr_addr), .b(12'h305), .eq(sel_mtvec));  // open: gt, lt
  Comparator #(.width(12)) comparator_4 (.a(csr_addr), .b(12'h341), .eq(sel_mepc));  // open: gt, lt
  Comparator #(.width(12)) comparator_5 (.a(csr_addr), .b(12'h342), .eq(sel_mcause));  // open: gt, lt
  Multiplexer #(.width(32)) multiplexer_1 (
    .in0(32'h80000007), .in1(32'h8000000b), .out(multiplexer_1_out), .sel(irq_ext));
  Multiplexer #(.select(2), .width(32)) multiplexer_2 (
    .in0(DataIn_computed),
    .in1({mstatus_mret[31:8], mstatus_MIE, mstatus_mret[6:4], 1'b0, mstatus_mret[2:0]}),
    .in2({mstatus_mret[31:8], 1'b1, mstatus_mret[6:4], MPIE_cur, mstatus_mret[2:0]}), .in3({32{1'b0}}),
    .out(multiplexer_2_out), .sel({mret, trap}));
  or or_1 (or_1_out, mret, trap, and_1_out);
  and and_1 (and_1_out, write, sel_mstatus);
  and and_2 (and_2_out, write, sel_mie);
  and and_3 (and_3_out, write, sel_mtvec);
  Multiplexer #(.width(32)) multiplexer_3 (.in0(DataIn_computed), .in1(trac_pc), .out(multiplexer_3_out), .sel(trap));
  or or_2 (or_2_out, trap, and_4_out);
  and and_4 (and_4_out, write, sel_mepc);
  Multiplexer #(.width(32)) multiplexer_4 (
    .in0(DataIn_computed), .in1(multiplexer_1_out), .out(multiplexer_4_out), .sel(trap));
  and and_5 (and_5_out, write, sel_mcause);
  Register #(.width(32)) mstatus (
    .D(multiplexer_2_out), .en(or_1_out),
    .Q({mstatus_mret[31:8], MPIE_cur, mstatus_mret[6:4], mstatus_MIE, mstatus_mret[2:0]}), .clk(CLK));  // open: clr
  Register #(.width(32)) mie (
    .D(DataIn_computed), .en(and_2_out), .Q({reg_mie_Q[31:12], MEIE, reg_mie_Q[10:8], MTIE, reg_mie_Q[6:0]}),
    .clk(CLK));  // open: clr
  Register #(.width(32)) mtvec (.D(DataIn_computed), .en(and_3_out), .Q(mtvec_out), .clk(CLK));  // open: clr
  Register #(.width(32)) mepc (.D(multiplexer_3_out), .en(or_2_out), .Q(mepc_out), .clk(CLK));  // open: clr
  Register #(.width(32)) mcause (.D(multiplexer_4_out), .en(or_3_out), .Q(reg_mcause_Q), .clk(CLK));  // open: clr
  or or_3 (or_3_out, trap, and_5_out);
  and and_6 (and_6_out, irq_ext, MEIE, mstatus_MIE);
  and and_7 (and_7_out, irq_timer, MTIE, mstatus_MIE);
  or or_4 (irq_pending, and_6_out, and_7_out);
  Multiplexer #(.select(3), .width(32)) multiplexer_5 (
    .in0({mstatus_mret[31:8], MPIE_cur, mstatus_mret[6:4], mstatus_MIE, mstatus_mret[2:0]}),
    .in1({reg_mie_Q[31:12], MEIE, reg_mie_Q[10:8], MTIE, reg_mie_Q[6:0]}), .in2(mtvec_out), .in3(mepc_out),
    .in4(reg_mcause_Q), .in5({32{1'b0}}), .in6({32{1'b0}}), .in7({32{1'b0}}), .out(DataOut),
    .sel({sel_mcause, or_6_out}));
  or or_5 (or_6_out[1], sel_mepc, sel_mtvec);
  or or_6 (or_6_out[0], sel_mepc, sel_mie);
  assign not_1_out = ~DataIn;  // NOT_Gate not_1, 32 bits wide
  assign OR_result = DataIn | DataOut;  // OR_Gate or_7, 32 bits wide
  assign AND_result = not_1_out & DataOut;  // AND_Gate and_8, 32 bits wide
  Multiplexer #(.select(3), .width(32)) multiplexer_6 (
    .in0({32{1'b0}}), .in1(DataIn), .in2(OR_result), .in3(AND_result), .in4({32{1'b0}}), .in5(DataIn),
    .in6(OR_result), .in7(AND_result), .out(DataIn_computed), .sel(funct3));

  // Other names for the same wires on the sheet: mstatus_trap (some bits) = {mstatus_mret[31:8], mstatus_MIE, mstatus_mret[6:4], mstatus_mret[2:0]};
  //   reg_mstatus_Q[31:0] = {mstatus_mret[31:8], MPIE_cur, mstatus_mret[6:4], mstatus_MIE, mstatus_mret[2:0]};
  //   mstatus_mret[3] = MPIE_cur; MIE_cur = mstatus_MIE; reg_mepc_Q[31:0] = mepc_out;
  //   reg_mie_Q (some bits) = {MEIE, MTIE}; reg_mtvec_Q[31:0] = mtvec_out; trap_pc[31:0] = trac_pc

  // Notes on the sheet:
  //   Interruptions hardware
endmodule

module UC_uC (
  input  [6:0] opcode,
  input  [2:0] funct3,
  input  [6:0] funct7,
  input  [2:0] Etat,
  input  Zero,
  input  ALUResult,
  input  mstatus_MIE,
  input  irq_pending,
  output MemAddrSrc,
  output ALUoutWrite,
  output IRWrite,
  output MemWrite,
  output PCWrite,
  output MARWrite,
  output RegWrite,
  output [2:0] PCSrc,
  output [2:0] WBSrc,
  output MDRWrite,
  output [2:0] ImmSrc,
  output ALUSrc,
  output RESET_CTR,
  output isAUIPC,
  output [3:0] ALUop,
  output write_csr,
  output mret,
  output trap
);

  wire and_4_out, and_5_out, and_6_out, and_7_out, and_8_out, and_9_out, and_10_out, and_11_out, and_12_out,
       and_13_out, and_14_out, and_15_out, auipc_wb, auipc_write, beq_taken, bge_taken, bgeu_taken,
       blt_taken, bltu_taken, bne_taken, branch_taken, branch_write, isBEQ, isBGE, isBGEU, isBLT, isBLTU,
       isBNE, isBranch, isCSR, isJALR, isLUI, isLW, isMRET, isMRET_funct7, isMUL, isState1, isState2,
       isState4, isSW, isTypeI, isTypeR, jal_wb, jal_write, jalr_wb, lui_wb, lw_wb, mret_state3, mret_write,
       not_1_out, not_2_out, not_4_out, NOT_Zero, or_3_out, trap_write, typeI_wb, typeR_wb;
  wire [1:1] or_8_out;
  wire [3:0] ALUop_t;
  wire [3:3] multiplexer_1_out;

  Decoder #(.select(3)) decoder_1 (
    .out0(ALUoutWrite), .out1(isState1), .out2(isState2), .out3(MemAddrSrc), .out4(isState4), .sel(Etat),
    .en(1'b1));  // open: out5, out6, out7
  // Probe on 7'b0010011
  // Probe on 7'b0000011
  // Probe on 7'b0100011
  // Probe on 7'b1100011
  // Probe on 7'b1101111
  // Probe on 7'b1110011
  // Probe on 7'b0110000
  Comparator #(.width(7)) comparator_1 (.a(opcode), .b(7'b0110011), .eq(isTypeR));  // open: gt, lt
  // Probe on 7'b0110011
  Comparator #(.width(7)) comparator_2 (.a(opcode), .b(7'b0010011), .eq(isTypeI));  // open: gt, lt
  Comparator #(.width(7)) comparator_3 (.a(opcode), .b(7'b0000011), .eq(isLW));  // open: gt, lt
  Comparator #(.width(7)) comparator_4 (.a(opcode), .b(7'b0100011), .eq(isSW));  // open: gt, lt
  Comparator #(.width(7)) comparator_5 (.a(opcode), .b(7'b1100011), .eq(isBranch));  // open: gt, lt
  Comparator #(.width(7)) comparator_6 (.a(opcode), .b(7'b1101111), .eq(ImmSrc[2]));  // open: gt, lt
  Comparator #(.width(7)) comparator_7 (.a(opcode), .b(7'b1100111), .eq(isJALR));  // open: gt, lt
  // Probe on 7'b1100111
  Comparator #(.width(7)) comparator_8 (.a(opcode), .b(7'b0110111), .eq(isLUI));  // open: gt, lt
  // Probe on 7'b0110111
  Comparator #(.width(7)) comparator_9 (.a(opcode), .b(7'b0010111), .eq(isAUIPC));  // open: gt, lt
  // Probe on 7'b0010111
  and and_1 (isMUL, isTypeR, funct7[0]);
  Comparator #(.width(7)) comparator_10 (.a(opcode), .b(7'b1110011), .eq(isCSR));  // open: gt, lt
  Comparator #(.width(7)) comparator_11 (.a(funct7), .b(7'b0110000), .eq(isMRET_funct7));  // open: gt, lt
  and and_2 (isMRET, isCSR, isMRET_funct7);
  and and_3 (MDRWrite, MemAddrSrc, isLW);
  or or_1 (ALUSrc, isTypeI, isLW, isSW, isJALR, isLUI, isAUIPC);
  and and_4 (and_4_out, isTypeR, isState4);
  and and_5 (and_5_out, isState4, isTypeI);
  and and_6 (and_6_out, isState2, isBranch);
  and and_7 (and_7_out, isState4, ImmSrc[2]);
  and and_8 (and_8_out, isState4, isJALR);
  and and_9 (and_9_out, isState4, isLUI);
  and and_10 (and_10_out, isState4, isAUIPC);
  and and_11 (and_11_out, MemAddrSrc, isSW);
  and and_12 (and_12_out, isState4, isLW);
  and and_13 (and_13_out, isState4, isCSR, not_1_out);
  not not_1 (not_1_out, isMRET);
  and and_14 (and_14_out, isState2, isMRET);
  and and_15 (and_15_out, isState1, trap);
  Multiplexer multiplexer_1 (.in0(1'b0), .in1(funct7[5]), .out(multiplexer_1_out[3]), .sel(isTypeR));
  ROM #(.addrWidth(4), .dataWidth(4)) rom_1 (.addr({multiplexer_1_out[3], funct3}), .data(ALUop_t));
  not not_2 (not_2_out, isMRET);
  or or_2 (RESET_CTR, and_4_out, and_5_out, and_6_out, and_7_out, and_8_out, and_9_out, and_10_out, and_11_out, and_12_out, and_13_out, and_14_out, and_15_out);
  and and_16 (write_csr, isCSR, not_2_out, isState2);
  and and_17 (mret, isMRET, isState2);
  and and_18 (trap, mstatus_MIE, irq_pending, isState1);
  // Probe on ALUop_t
  or or_3 (or_3_out, isSW, isLW);
  or or_4 (PCSrc[2], trap_write, mret_write);
  or or_5 (ImmSrc[0], isSW, isLUI, isAUIPC);
  or or_6 (ImmSrc[1], isBranch, isLUI, isAUIPC);
  and and_19 (MemWrite, MemAddrSrc, isSW);
  and and_20 (MARWrite, isState2, or_3_out);
  or or_7 (PCSrc[0], jal_write, branch_write, auipc_write, mret_write);
  or or_8 (or_8_out[1], isLW, isSW, isJALR, isLUI, isAUIPC);
  Multiplexer #(.select(2), .width(4)) multiplexer_2 (
    .in0(ALUop_t), .in1(4'b1010), .in2(4'b0000), .in3(4'b0000), .out(ALUop), .sel({or_8_out[1], isMUL}));
  and and_21 (mret_state3, mret, MemAddrSrc);
  Comparator #(.width(3)) comparator_12 (.a(funct3), .b(3'b000), .eq(isBEQ));  // open: gt, lt
  Comparator #(.width(3)) comparator_13 (.a(funct3), .b(3'b001), .eq(isBNE));  // open: gt, lt
  Comparator #(.width(3)) comparator_14 (.a(funct3), .b(3'b100), .eq(isBLT));  // open: gt, lt
  Comparator #(.width(3)) comparator_15 (.a(funct3), .b(3'b101), .eq(isBGE));  // open: gt, lt
  Comparator #(.width(3)) comparator_16 (.a(funct3), .b(3'b110), .eq(isBLTU));  // open: gt, lt
  Comparator #(.width(3)) comparator_17 (.a(funct3), .b(3'b111), .eq(isBGEU));  // open: gt, lt
  and and_22 (jal_write, isState2, ImmSrc[2]);
  and and_23 (PCSrc[1], isState2, isJALR);
  and and_24 (branch_write, isState2, isBranch, branch_taken);
  and and_25 (auipc_write, isState2, isAUIPC);
  and and_26 (trap_write, isState1, trap);
  and and_27 (mret_write, isState2, mret);
  not not_3 (NOT_Zero, Zero);
  and and_28 (beq_taken, isBEQ, Zero);
  and and_29 (bne_taken, isBNE, NOT_Zero);
  and and_30 (blt_taken, isBLT, Zero);
  and and_31 (bge_taken, isBGE, NOT_Zero);
  and and_32 (bltu_taken, isBLTU, Zero);
  and and_33 (bgeu_taken, isBGEU, NOT_Zero);
  or or_9 (PCWrite, ALUoutWrite, jal_write, PCSrc[1], branch_write, auipc_write, trap_write, mret_write);
  or or_10 (branch_taken, beq_taken, bne_taken, blt_taken, bge_taken, bltu_taken, bgeu_taken);
  not not_4 (not_4_out, isMRET);
  and and_34 (typeR_wb, isTypeR, isState4);
  and and_35 (typeI_wb, isState4, isTypeI);
  and and_36 (lw_wb, isState4, isLW);
  and and_37 (jal_wb, isState4, ImmSrc[2]);
  and and_38 (jalr_wb, isState4, isJALR);
  and and_39 (lui_wb, isState4, isLUI);
  and and_40 (auipc_wb, isState4, isAUIPC);
  and and_41 (WBSrc[2], isCSR, not_4_out, isState4);
  or or_11 (WBSrc[0], lw_wb, lui_wb);
  or or_12 (WBSrc[1], jal_wb, jalr_wb, lui_wb);
  or or_13 (RegWrite, typeR_wb, typeI_wb, lw_wb, jal_wb, jalr_wb, lui_wb, auipc_wb, WBSrc[2]);

  assign IRWrite = ALUoutWrite;

  // Other names for the same wires on the sheet: funct3_0 = funct3[0]; funct3_1 = funct3[1]; funct3_2 = funct3[2];
  //   funct7bit25 = funct7[0]; funct7bit30 = funct7[5]; isJAL = ImmSrc[2]; isState0 = ALUoutWrite;
  //   isState3 = MemAddrSrc; jalr_write = PCSrc[1]; csr_wb = WBSrc[2]

  // Notes on the sheet:
  //   Fetch
  //   Decode
  //   isTypeR
  //   isTypeI
  //   isLW
  //   isSW
  //   isBranch
  //   isJAL
  //   isMUL has same opcode as type R
  //   isCSR
  //   isMRET_funct7
  //   Execute
  //   isJALR
  //   isLUI
  //   isAUIPC
  //   Memory
  //   Writeback
  //   contents of rom_1 (hex, n*v repeats v):
  //   0 5 8 9 4 6 3 2 1 4*0 7
endmodule

module uController (
  input  CLK_Manual,
  output [31:0] S,
  output [31:0] out_3
);

  wire ALUoutWrite, ALUResult, ALUSrc, and_2_out, and_5_out, and_6_out, and_7_out, and_8_out, and_9_out,
       and_10_out, and_11_out, and_12_out, and_13_out, and_14_out, btn_any, btn_prev, CLK, comparator_3_eq,
       comparator_3_gt, comparator_4_eq, comparator_4_lt, display_1_plus_minus, irq_ext, irq_pending,
       irq_timer, IRWrite, isAUIPC, MARWrite, MDRWrite, MemAddrSrc, MemWrite, mret, mstatus_MIE, not_1_out,
       not_2_out, or_1_out, or_2_out, PC_oldwrite, PCWrite, register_1_q, RegWrite, RESET_CTR, sel_button,
       sel_counter, sel_led, sel_led_col0, sel_led_col1, sel_led_col2, sel_led_col3, sel_led_col4,
       sel_led_col5, sel_led_col6, sel_led_col7, sel_led_col8, sel_led_col9, sel_ram, trap, write_csr, Zero;
  wire [2:0] Etat, funct3, ImmSrc, PCSrc, WBSrc;
  wire [3:0] ALUop, button_input, display_1_d0, display_1_d1, display_1_d2, display_1_d3, display_1_d4,
       display_1_d5, display_1_d6, display_1_d7, display_1_d8, display_1_d9;
  wire [4:0] imm_csr, rd;
  wire [6:0] opcode;
  wire [11:0] csr_addr;
  wire [13:0] multiplexer_1_out, shifter_3_out;
  wire [17:0] shifter_3_out_2;
  wire [19:0] register_2_q, register_3_q, register_4_q, register_5_q, register_6_q, register_7_q,
       register_8_q, register_9_q, register_10_q, register_11_q;
  wire [31:0] adder_1_out, adder_2_out, adder_3_out, and_4_out, Counter_Q_q, DataOut, ImmExt,
       Instruction_Data_RAM_dout, loadextender_1_load_data, MAR_q, MDR_q, mepc_out, mtvec_out,
       multiplexer_2_out, multiplexer_3_out, multiplexer_4_out, multiplexer_5_out, multiplexer_6_out, PC_old,
       PC_q, registerfile_1_s12, registerfile_1_sa, SB, shifter_1_out, shifter_2_out,
       storemerger_1_store_data, subtractor_1_out;
  wire [31:1] alu_1_s;

  Register #(.width(32)) MAR (.D({alu_1_s, ALUResult}), .en(MARWrite), .Q(MAR_q), .clk(CLK));  // open: clr
  Comparator #(.width(32)) comparator_1 (.a(MAR_q), .b(32'h10000), .lt(sel_ram));  // open: gt, eq
  Comparator #(.width(32)) comparator_2 (.a(MAR_q), .b(32'h10000), .eq(sel_button));  // open: gt, lt
  Comparator #(.width(32)) comparator_3 (
    .a(MAR_q), .b(32'h10004), .gt(comparator_3_gt), .eq(comparator_3_eq));  // open: lt
  Comparator #(.width(32)) comparator_4 (
    .a(MAR_q), .b(32'h10028), .eq(comparator_4_eq), .lt(comparator_4_lt));  // open: gt
  Comparator #(.width(32)) comparator_5 (.a(MAR_q), .b(32'h1002c), .eq(sel_counter));  // open: gt, lt
  Subtractor #(.width(32)) subtractor_1 (.a(MAR_q), .b(32'h10004), .out(subtractor_1_out));  // open: bin, bout
  Shifter #(.shift("lr"), .width(32)) shifter_1 (.in(MAR_q), .\dist (5'b00010), .out(shifter_1_out));
  or or_1 (or_1_out, comparator_3_gt, comparator_3_eq);
  or or_2 (or_2_out, comparator_4_eq, comparator_4_lt);
  Shifter #(.shift("lr"), .width(32)) shifter_2 (.in(subtractor_1_out), .\dist (5'b00010), .out(shifter_2_out));
  and and_1 (sel_led, or_1_out, or_2_out);
  Multiplexer #(.width(14)) multiplexer_1 (
    .in0(shifter_3_out), .in1(shifter_1_out[13:0]), .out(multiplexer_1_out), .sel(MemAddrSrc));
  and and_2 (and_2_out, MemWrite, sel_ram);
  Decoder #(.select(4)) decoder_1 (
    .out0(sel_led_col0), .out1(sel_led_col1), .out2(sel_led_col2), .out3(sel_led_col3), .out4(sel_led_col4),
    .out5(sel_led_col5), .out6(sel_led_col6), .out7(sel_led_col7), .out8(sel_led_col8), .out9(sel_led_col9),
    .sel(shifter_2_out[3:0]), .en(sel_led));  // open: out10, out11, out12, out13, out14, out15
  RAM #(.addrWidth(14), .asyncread("true"), .dataWidth(32), .\type ("nonvolatile")) Instruction_Data_RAM (
    .addr(multiplexer_1_out), .we(and_2_out), .oe(1'b1), .clk(CLK), .din(storemerger_1_store_data),
    .dout(Instruction_Data_RAM_dout));
  StoreMerger storemerger_1 (
    .RAM_data(Instruction_Data_RAM_dout), .SB_data(SB), .byte_offset(MAR_q[1:0]), .funct3(funct3),
    .store_data(storemerger_1_store_data));
  CSR_File csr_file_1 (
    .csr_addr(csr_addr), .DataIn(SB), .funct3(funct3), .write(write_csr), .CLK(CLK), .irq_ext(irq_ext),
    .irq_timer(irq_timer), .trac_pc(PC_old), .trap(trap), .mret(mret), .mstatus_MIE(mstatus_MIE),
    .irq_pending(irq_pending), .mtvec_out(mtvec_out), .DataOut(DataOut), .mepc_out(mepc_out));
  Register #(.width(32)) IR (
    .D(Instruction_Data_RAM_dout), .en(IRWrite), .Q({csr_addr, imm_csr, funct3, rd, opcode}), .clk(CLK));  // open: clr
  Counter #(.max('hffffffff), .width(32)) Counter_Q (
    .Q(Counter_Q_q), .clk(CLK));  // open: load, D, count, carry, up, clr
  Register #(.width(1)) register_1 (.D(Counter_Q_q[12]), .Q(register_1_q), .clk(CLK));  // open: en, clr
  LoadExtender loadextender_1 (
    .RAM_data(Instruction_Data_RAM_dout), .byte_offset(MAR_q[1:0]), .funct3(funct3),
    .load_data(loadextender_1_load_data));
  not not_1 (not_1_out, register_1_q);
  and and_3 (irq_timer, not_1_out, Counter_Q_q[12]);
  SignExtender signextender_1 (.IR({csr_addr, imm_csr, funct3, rd, opcode}), .ImmSrc(ImmSrc), .ImmExt(ImmExt));
  Clock u_CLK (.out(CLK));
  assign and_4_out = 32'hfffffffe & out_3;  // AND_Gate and_4, 32 bits wide
  Adder #(.width(32)) adder_1 (.a(PC_old), .b(ImmExt), .out(adder_1_out));  // open: cin, cout
  Multiplexer #(.select(2), .width(32)) multiplexer_2 (
    .in0(loadextender_1_load_data), .in1({{28{1'b0}}, button_input}), .in2(Counter_Q_q), .in3({32{1'b0}}),
    .out(multiplexer_2_out), .sel({sel_counter, sel_button}));
  Multiplexer #(.enable("true"), .select(3), .width(32)) multiplexer_3 (
    .in0(adder_2_out), .in1(adder_1_out), .in2(and_4_out), .in3({32{1'b0}}), .in4(mtvec_out), .in5(mepc_out),
    .in6({32{1'b0}}), .in7({32{1'b0}}), .out(multiplexer_3_out), .sel(PCSrc));  // open: en
  Register #(.width(32)) u_PC_old (.D(PC_q), .en(IRWrite), .Q(PC_old), .clk(CLK));  // open: clr
  Register #(.width(32)) PC (.D(multiplexer_3_out), .en(PCWrite), .Q(PC_q), .clk(CLK));  // open: clr
  Register #(.width(32)) MDR (.D(multiplexer_2_out), .en(MDRWrite), .Q(MDR_q), .clk(CLK));  // open: clr
  Counter #(.max('h7), .ongoal("continue"), .width(3)) UC_Counter (
    .load(RESET_CTR), .D(3'b000), .count(1'b1), .Q(Etat), .clk(CLK));  // open: carry, up, clr
  Shifter #(.shift("lr"), .width(32)) shifter_3 (.in(PC_q), .\dist (5'b00010), .out({shifter_3_out_2, shifter_3_out}));
  Control_Unit control_unit_1 (
    .opcode(opcode), .funct3(funct3), .funct7(csr_addr[11:5]), .Zero(Zero), .ALUResult(ALUResult),
    .Etat(Etat), .IRWrite(IRWrite), .PC_oldwrite(PC_oldwrite), .PCWrite(PCWrite), .PCSrc(PCSrc),
    .MemAddrSrc(MemAddrSrc), .ImmSrc(ImmSrc), .ALUSrc(ALUSrc), .ALUoutWrite(ALUoutWrite),
    .MDRWrite(MDRWrite), .MARWrite(MARWrite), .MemWrite(MemWrite), .WBSrc(WBSrc), .RegWrite(RegWrite),
    .isAUIPC(isAUIPC), .RESET_CTR(RESET_CTR), .ALUop(ALUop));
  and and_5 (and_5_out, MemWrite, sel_led, sel_led_col0);
  and and_6 (and_6_out, MemWrite, sel_led, sel_led_col1);
  and and_7 (and_7_out, MemWrite, sel_led, sel_led_col2);
  and and_8 (and_8_out, MemWrite, sel_led, sel_led_col3);
  and and_9 (and_9_out, MemWrite, sel_led, sel_led_col4);
  and and_10 (and_10_out, MemWrite, sel_led, sel_led_col5);
  and and_11 (and_11_out, MemWrite, sel_led, sel_led_col6);
  and and_12 (and_12_out, MemWrite, sel_led, sel_led_col7);
  and and_13 (and_13_out, MemWrite, sel_led, sel_led_col8);
  and and_14 (and_14_out, MemWrite, sel_led, sel_led_col9);
  Adder #(.width(32)) adder_2 (.a(PC_q), .b(32'h4), .out(adder_2_out));  // open: cin, cout
  // Probe on out_3
  Register #(.width(20)) register_2 (.D(SB[19:0]), .en(and_5_out), .Q(register_2_q), .clk(CLK));  // open: clr
  Register #(.width(20)) register_3 (.D(SB[19:0]), .en(and_6_out), .Q(register_3_q), .clk(CLK));  // open: clr
  Register #(.width(20)) register_4 (.D(SB[19:0]), .en(and_7_out), .Q(register_4_q), .clk(CLK));  // open: clr
  Register #(.width(20)) register_5 (.D(SB[19:0]), .en(and_8_out), .Q(register_5_q), .clk(CLK));  // open: clr
  Register #(.width(20)) register_6 (.D(SB[19:0]), .en(and_9_out), .Q(register_6_q), .clk(CLK));  // open: clr
  Register #(.width(20)) register_7 (.D(SB[19:0]), .en(and_10_out), .Q(register_7_q), .clk(CLK));  // open: clr
  Register #(.width(20)) register_8 (.D(SB[19:0]), .en(and_11_out), .Q(register_8_q), .clk(CLK));  // open: clr
  Register #(.width(20)) register_9 (.D(SB[19:0]), .en(and_12_out), .Q(register_9_q), .clk(CLK));  // open: clr
  Register #(.width(20)) register_10 (.D(SB[19:0]), .en(and_13_out), .Q(register_10_q), .clk(CLK));  // open: clr
  Register #(.width(20)) register_11 (.D(SB[19:0]), .en(and_14_out), .Q(register_11_q), .clk(CLK));  // open: clr
  Adder #(.width(32)) adder_3 (.a(PC_old), .b(32'h4), .out(adder_3_out));  // open: cin, cout
  // Probe on WBSrc
  DotMatrix #(.matrixcols(10), .matrixrows(20)) dotmatrix_1 (
    .col0(register_2_q), .col1(register_3_q), .col2(register_4_q), .col3(register_5_q), .col4(register_6_q),
    .col5(register_7_q), .col6(register_8_q), .col7(register_9_q), .col8(register_10_q), .col9(register_11_q));
  Multiplexer #(.enable("true"), .select(3), .width(32)) multiplexer_4 (
    .in0(out_3), .in1(MDR_q), .in2(adder_3_out), .in3(ImmExt), .in4(DataOut), .in5({32{1'b0}}),
    .in6({32{1'b0}}), .in7({32{1'b0}}), .out(multiplexer_4_out), .sel(WBSrc));  // open: en
  _7_Segment_Display u_7_segment_display_1 (.g(display_1_plus_minus));  // open: f, a, b, e, d, c, dp
  Button button_1 (.out(button_input[2]));
  Button button_2 (.out(button_input[0]));
  Button button_3 (.out(button_input[1]));
  Button button_4 (.out(button_input[3]));
  // Probe on {{28{1'b0}}, button_input}
  Hex_Digit_Display hex_digit_display_1 (.value(display_1_d9));  // open: dp
  display display_1 (
    .E(registerfile_1_s12), .plus_minus(display_1_plus_minus), .d9(display_1_d9), .d8(display_1_d8),
    .d7(display_1_d7), .d6(display_1_d6), .d5(display_1_d5), .d4(display_1_d4), .d3(display_1_d3),
    .d2(display_1_d2), .d1(display_1_d1), .d0(display_1_d0));
  Hex_Digit_Display hex_digit_display_2 (.value(display_1_d8));  // open: dp
  Hex_Digit_Display hex_digit_display_3 (.value(display_1_d7));  // open: dp
  RegisterFile registerfile_1 (
    .rd(rd), .rs1(imm_csr), .rs2(csr_addr[4:0]), .RegWrite(RegWrite), .CLK(CLK), .Data(multiplexer_4_out),
    .SA(registerfile_1_sa), .SB(SB), .S12(registerfile_1_s12));
  or or_3 (btn_any, button_input[1], button_input[0], button_input[3], button_input[2]);
  Hex_Digit_Display hex_digit_display_4 (.value(display_1_d6));  // open: dp
  Register #(.width(1)) register_12 (.D(btn_any), .Q(btn_prev), .clk(CLK));  // open: en, clr
  Hex_Digit_Display hex_digit_display_5 (.value(display_1_d5));  // open: dp
  not not_2 (not_2_out, btn_prev);
  Hex_Digit_Display hex_digit_display_6 (.value(display_1_d4));  // open: dp
  Hex_Digit_Display hex_digit_display_7 (.value(display_1_d3));  // open: dp
  and and_15 (irq_ext, not_2_out, btn_any);
  Hex_Digit_Display hex_digit_display_8 (.value(display_1_d2));  // open: dp
  Hex_Digit_Display hex_digit_display_9 (.value(display_1_d1));  // open: dp
  Hex_Digit_Display hex_digit_display_10 (.value(display_1_d0));  // open: dp
  Multiplexer #(.width(32)) multiplexer_5 (
    .in0(registerfile_1_sa), .in1(PC_old), .out(multiplexer_5_out), .sel(isAUIPC));
  Multiplexer #(.enable("true"), .width(32)) multiplexer_6 (
    .in0(SB), .in1(ImmExt), .out(multiplexer_6_out), .sel(ALUSrc));  // open: en
  ALU alu_1 (.A(multiplexer_5_out), .B(multiplexer_6_out), .OP(ALUop), .S({alu_1_s, ALUResult}), .Zero(Zero));
  Register #(.width(32)) ALUout (.D({alu_1_s, ALUResult}), .en(ALUoutWrite), .Q(out_3), .clk(CLK));  // open: clr

  assign S = out_3;

  // Other names for the same wires on the sheet: rs1[4:0] = imm_csr; rs2[4:0] = csr_addr[4:0];
  //   funct7[6:0] = csr_addr[11:5]

  // Notes on the sheet:
  //   State 0: Fetch 
  //   State 1: Decode
  //   State2 : Execute
  //   State 3 : Memory
  //   State 4 : Writeback
  //   sel_joystick
endmodule

module LoadExtender (
  input  [31:0] RAM_data,
  input  [1:0] byte_offset,
  input  [2:0] funct3,
  output [31:0] load_data
);

  wire [7:0] extracted_byte;
  wire [15:0] extracted_half;
  wire [31:0] byte_signed, byte_unsigned, extended_byte, extended_half, half_signed, half_unsigned;

  Multiplexer #(.select(2), .width(8)) multiplexer_1 (
    .in0(RAM_data[7:0]), .in1(RAM_data[15:8]), .in2(RAM_data[23:16]), .in3(RAM_data[31:24]),
    .out(extracted_byte), .sel(byte_offset));
  Multiplexer #(.width(16)) multiplexer_2 (
    .in0(RAM_data[15:0]), .in1(RAM_data[31:16]), .out(extracted_half), .sel(byte_offset[1]));
  assign byte_signed = {{24{extracted_byte[7]}}, extracted_byte};  // Bit_Extender bit_extender_1
  assign byte_unsigned = {{24{1'b0}}, extracted_byte};  // Bit_Extender bit_extender_2
  Multiplexer #(.width(32)) multiplexer_3 (
    .in0(byte_signed), .in1(byte_unsigned), .out(extended_byte), .sel(funct3[2]));
  Multiplexer #(.select(2), .width(32)) multiplexer_4 (
    .in0(extended_byte), .in1(extended_half), .in2(RAM_data), .in3({32{1'b0}}), .out(load_data),
    .sel(funct3[1:0]));
  assign half_signed = {{16{extracted_half[15]}}, extracted_half};  // Bit_Extender bit_extender_3
  assign half_unsigned = {{16{1'b0}}, extracted_half};  // Bit_Extender bit_extender_4
  Multiplexer #(.width(32)) multiplexer_5 (
    .in0(half_signed), .in1(half_unsigned), .out(extended_half), .sel(funct3[2]));

  // Other names for the same wires on the sheet: funct3_0 = funct3[0]; funct3_1 = funct3[1]; funct3_2 = funct3[2]
endmodule

module StoreMerger (
  input  [31:0] RAM_data,
  input  [31:0] SB_data,
  input  [1:0] byte_offset,
  input  [2:0] funct3,
  output [31:0] store_data
);

  wire sel0, sel1, sel2, sel3;
  wire [31:0] bytes_fused, half_fused;

  Decoder #(.select(2)) decoder_1 (.out0(sel0), .out1(sel1), .out2(sel2), .out3(sel3), .sel(byte_offset));  // open: en
  Multiplexer #(.width(8)) multiplexer_1 (.in0(RAM_data[7:0]), .in1(SB_data[7:0]), .out(bytes_fused[7:0]), .sel(sel0));
  Multiplexer #(.width(8)) multiplexer_2 (
    .in0(RAM_data[15:8]), .in1(SB_data[7:0]), .out(bytes_fused[15:8]), .sel(sel1));
  Multiplexer #(.width(8)) multiplexer_3 (
    .in0(RAM_data[23:16]), .in1(SB_data[7:0]), .out(bytes_fused[23:16]), .sel(sel2));
  Multiplexer #(.width(8)) multiplexer_4 (
    .in0(RAM_data[31:24]), .in1(SB_data[7:0]), .out(bytes_fused[31:24]), .sel(sel3));
  Multiplexer #(.width(32)) multiplexer_5 (
    .in0({RAM_data[31:16], SB_data[15:0]}), .in1({SB_data[15:0], RAM_data[15:0]}), .out(half_fused),
    .sel(byte_offset[1]));
  Multiplexer #(.select(2), .width(32)) multiplexer_6 (
    .in0(bytes_fused), .in1(half_fused), .in2(SB_data), .in3({32{1'b0}}), .out(store_data), .sel(funct3[1:0]));

  // Other names for the same wires on the sheet: ram_2[7:0] = RAM_data[23:16]; ram_high[15:0] = RAM_data[31:16];
  //   ram_3[7:0] = RAM_data[31:24]; funct_3[2:0] = funct3; funct_3_0 = funct3[0]; funct_3_1 = funct3[1];
  //   ram_0[7:0] = RAM_data[7:0]; ram_low[15:0] = RAM_data[15:0]; ram_1[7:0] = RAM_data[15:8];
  //   sb0[7:0] = SB_data[7:0]; sb_low[15:0] = SB_data[15:0]; sb1[7:0] = SB_data[15:8]; byte_offset_0 = byte_offset[0];
  //   byte_offset_1 = byte_offset[1]; merged_byte_0[7:0] = bytes_fused[7:0]; merged_byte_1[7:0] = bytes_fused[15:8];
  //   merged_byte_2[7:0] = bytes_fused[23:16]; merged_byte_3[7:0] = bytes_fused[31:24]; funct_3_2 = funct3[2];
  //   sb2[7:0] = SB_data[23:16]; sb_high[15:0] = SB_data[31:16]; sb3[7:0] = SB_data[31:24]
endmodule

module Control_Unit (
  input  [6:0] opcode,
  input  [2:0] funct3,
  input  [6:0] funct7,
  input  Zero,
  input  ALUResult,
  input  [2:0] Etat,
  output IRWrite,
  output PC_oldwrite,
  output PCWrite,
  output [2:0] PCSrc,
  output MemAddrSrc,
  output [2:0] ImmSrc,
  output ALUSrc,
  output ALUoutWrite,
  output MDRWrite,
  output MARWrite,
  output MemWrite,
  output [2:0] WBSrc,
  output RegWrite,
  output isAUIPC,
  output RESET_CTR,
  output [3:0] ALUop
);

  wire and_5_out, and_6_out, and_7_out, and_8_out, and_10_out, and_14_out, and_15_out, and_16_out,
       bit5_gated, branch_taken, funct3_000, funct3_001, funct3_101, isBranch, isLUI, isLW, isMUL,
       isShiftImm, isState1, isState4, isSW, isTypeI, isTypeR, isTypeR_nonMUL, multiplexer_1_out, not_1_out,
       or_1_out, or_2_out, or_5_out, or_10_out, or_12_out, or_13_out;
  wire [3:0] multiplexer_3_out, multiplexer_4_out, raw_branch_op, ROM_out;

  Decoder #(.select(3)) decoder_1 (
    .out0(IRWrite), .out1(isState1), .out2(ALUoutWrite), .out3(MemAddrSrc), .out4(isState4), .sel(Etat),
    .en(1'b1));  // open: out5, out6, out7
  Comparator #(.width(7)) comparator_1 (.a(opcode), .b(7'b0110011), .eq(isTypeR));  // open: gt, lt
  // Probe on 7'b0110011
  Comparator #(.width(7)) comparator_2 (.a(opcode), .b(7'b0010011), .eq(isTypeI));  // open: gt, lt
  // Probe on 7'b0010011
  Comparator #(.width(7)) comparator_3 (.a(opcode), .b(7'b0000011), .eq(isLW));  // open: gt, lt
  // Probe on 7'b0000011
  Comparator #(.width(7)) comparator_4 (.a(opcode), .b(7'b0100011), .eq(isSW));  // open: gt, lt
  // Probe on 7'b0100011
  Comparator #(.width(7)) comparator_5 (.a(opcode), .b(7'b1100011), .eq(isBranch));  // open: gt, lt
  // Probe on 7'b1100011
  Comparator #(.width(7)) comparator_6 (.a(opcode), .b(7'b1101111), .eq(ImmSrc[2]));  // open: gt, lt
  // Probe on 7'b1101111
  Comparator #(.width(7)) comparator_7 (.a(opcode), .b(7'b1100111), .eq(PCSrc[1]));  // open: gt, lt
  // Probe on 7'b1100111
  Comparator #(.width(7)) comparator_8 (.a(opcode), .b(7'b0110111), .eq(isLUI));  // open: gt, lt
  // Probe on 7'b0110111
  Comparator #(.width(7)) comparator_9 (.a(opcode), .b(7'b0010111), .eq(isAUIPC));  // open: gt, lt
  // Probe on 7'b0010111
  and and_1 (isMUL, isTypeR, funct3_000, funct7[0]);
  Multiplexer multiplexer_1 (.in0(Zero), .in1(ALUResult), .out(multiplexer_1_out), .sel(funct3[2]));
  xor xor_1 (branch_taken, funct3[0], multiplexer_1_out);
  Comparator #(.mode("unsigned"), .width(3)) comparator_10 (.a(funct3), .b(3'b001), .eq(funct3_001));  // open: gt, lt
  Comparator #(.mode("unsigned"), .width(3)) comparator_11 (.a(funct3), .b(3'b101), .eq(funct3_101));  // open: gt, lt
  Comparator #(.mode("unsigned"), .width(3)) comparator_12 (.a(funct3), .b(3'b000), .eq(funct3_000));  // open: gt, lt
  ROM #(.addrWidth(4), .dataWidth(4)) ALUop_rom (.addr({bit5_gated, funct3}), .data(ROM_out));
  not not_1 (not_1_out, isMUL);
  or or_1 (or_1_out, funct3_001, funct3_101);
  or or_2 (or_2_out, isTypeR_nonMUL, isShiftImm);
  and and_2 (isTypeR_nonMUL, isTypeR, not_1_out);
  and and_3 (isShiftImm, or_1_out, isTypeI);
  and and_4 (bit5_gated, or_2_out, funct7[5]);
  Multiplexer #(.select(2), .width(4)) multiplexer_2 (
    .in0(4'b0001), .in1(4'b0000), .in2(4'b1000), .in3(4'b1001), .out(raw_branch_op), .sel(funct3[2:1]));
  and and_5 (and_5_out, ALUoutWrite, isBranch, branch_taken);
  and and_6 (and_6_out, ALUoutWrite, isBranch, branch_taken);
  and and_7 (and_7_out, isState4, ImmSrc[2]);
  or or_3 (ImmSrc[0], isSW, isLUI, isAUIPC);
  or or_4 (ImmSrc[1], isBranch, isLUI, isAUIPC);
  or or_5 (or_5_out, isLW, isSW);
  and and_8 (and_8_out, isState4, ImmSrc[2]);
  or or_6 (PCSrc[0], and_6_out, and_7_out);
  or or_7 (ALUSrc, isTypeI, isLW, isSW, PCSrc[1], isAUIPC);
  and and_9 (MARWrite, ALUoutWrite, or_5_out);
  Multiplexer #(.width(4)) multiplexer_3 (.in0(4'b0000), .in1(raw_branch_op), .out(multiplexer_3_out), .sel(isBranch));
  and and_10 (and_10_out, isState4, PCSrc[1]);
  or or_8 (WBSrc[0], isLW, isLUI);
  or or_9 (WBSrc[1], ImmSrc[2], PCSrc[1], isLUI);
  Multiplexer #(.width(4)) multiplexer_4 (
    .in0(multiplexer_3_out), .in1(ROM_out), .out(multiplexer_4_out), .sel(or_10_out));
  or or_10 (or_10_out, isTypeR_nonMUL, isTypeI);
  or or_11 (PCWrite, IRWrite, and_5_out, and_8_out, and_10_out);
  Multiplexer #(.width(4)) multiplexer_5 (.in0(multiplexer_4_out), .in1(4'b1010), .out(ALUop), .sel(isMUL));
  and and_11 (MDRWrite, MemAddrSrc, isLW);
  and and_12 (MemWrite, MemAddrSrc, isSW);
  or or_12 (or_12_out, isTypeR, isTypeI, ImmSrc[2], PCSrc[1], isLUI, isAUIPC, isLW);
  and and_13 (RegWrite, isState4, or_12_out);
  and and_14 (and_14_out, ALUoutWrite, isBranch);
  and and_15 (and_15_out, MemAddrSrc, isSW);
  and and_16 (and_16_out, isState4, or_13_out);
  or or_13 (or_13_out, isTypeR, isTypeI, ImmSrc[2], PCSrc[1], isLUI, isAUIPC, isLW);
  or or_14 (RESET_CTR, and_14_out, and_15_out, and_16_out);

  assign PC_oldwrite = IRWrite;
  assign PCSrc[2] = 1'b0;
  assign WBSrc[2] = 1'b0;

  // Other names for the same wires on the sheet: funct3_0 = funct3[0]; funct3_1 = funct3[1]; funct3_2 = funct3[2];
  //   funct7bit25 = funct7[0]; funct7bit30 = funct7[5]; isJAL = ImmSrc[2]; isState0 = IRWrite; isState2 = ALUoutWrite;
  //   isState3 = MemAddrSrc; isJALR = PCSrc[1]

  // Notes on the sheet:
  //   Fetch
  //   Decode
  //   isMUL has same opcode as type R
  //   Execute
  //   isTypeR
  //   isTypeI
  //   isLoad
  //   isStore
  //   isBranch
  //   isJAL
  //   isJALR
  //   isLUI
  //   isAUIPC
  //   Memory
  //   Writeback
  //   contents of ALUop_rom (hex, n*v repeats v):
  //   0 5 8 9 4 6 3 2 1 4*0 7
endmodule

module display (
  input  [31:0] E,
  output plus_minus,
  output [3:0] d9,
  output [3:0] d8,
  output [3:0] d7,
  output [3:0] d6,
  output [3:0] d5,
  output [3:0] d4,
  output [3:0] d3,
  output [3:0] d2,
  output [3:0] d1,
  output [3:0] d0
);

  wire [31:0] divider_1_out, divider_2_out, divider_3_out, divider_4_out, divider_5_out, divider_6_out,
       divider_7_out, divider_8_out, divider_9_out, multiplexer_1_out, negator_1_out;
  wire [31:4] divider_1_rem, divider_2_rem, divider_3_rem, divider_4_rem, divider_5_rem, divider_6_rem,
       divider_7_rem, divider_8_rem, divider_9_rem, divider_10_rem;

  // Probe on E
  Negator #(.width(32)) negator_1 (.in(E), .out(negator_1_out));
  // Probe on negator_1_out
  Multiplexer #(.enable("true"), .width(32)) multiplexer_1 (
    .in0(E), .in1(negator_1_out), .out(multiplexer_1_out), .sel(E[31]));  // open: en
  Divider #(.width(32)) divider_1 (
    .a(multiplexer_1_out), .b(32'ha), .out(divider_1_out), .upper({32{1'b0}}), .rem({divider_1_rem, d0}));
  Divider #(.width(32)) divider_2 (
    .a(divider_1_out), .b(32'ha), .out(divider_2_out), .upper({32{1'b0}}), .rem({divider_2_rem, d1}));
  Divider #(.width(32)) divider_3 (
    .a(divider_2_out), .b(32'ha), .out(divider_3_out), .upper({32{1'b0}}), .rem({divider_3_rem, d2}));
  Divider #(.width(32)) divider_4 (
    .a(divider_3_out), .b(32'ha), .out(divider_4_out), .upper({32{1'b0}}), .rem({divider_4_rem, d3}));
  Divider #(.width(32)) divider_5 (
    .a(divider_4_out), .b(32'ha), .out(divider_5_out), .upper({32{1'b0}}), .rem({divider_5_rem, d4}));
  Divider #(.width(32)) divider_6 (
    .a(divider_5_out), .b(32'ha), .out(divider_6_out), .upper({32{1'b0}}), .rem({divider_6_rem, d5}));
  Divider #(.width(32)) divider_7 (
    .a(divider_6_out), .b(32'ha), .out(divider_7_out), .upper({32{1'b0}}), .rem({divider_7_rem, d6}));
  Divider #(.width(32)) divider_8 (
    .a(divider_7_out), .b(32'ha), .out(divider_8_out), .upper({32{1'b0}}), .rem({divider_8_rem, d7}));
  Divider #(.width(32)) divider_9 (
    .a(divider_8_out), .b(32'ha), .out(divider_9_out), .upper({32{1'b0}}), .rem({divider_9_rem, d8}));
  Divider #(.width(32)) divider_10 (
    .a(divider_9_out), .b(32'ha), .upper({32{1'b0}}), .rem({divider_10_rem, d9}));  // open: out

  assign plus_minus = E[31];
endmodule
